# Fritzing sketch ESParkle (saved by Fritzing 0.9.3b)
breadboards: 1

parts:
  WeMos_D1_Mini1 = WeMos D1 Mini
  5V = Power plug
  SP1 = SPEAKER [package=pcb_mount_speaker]
  Composant4 = NeoPixel Jewel [part_number=2226]
  Composant1 = Adafruit MAX98357A I2S 3W Class D Amplifier [part_number="Adafruit #3006"]
  GY1 = MPU-6050 Board GY-521 [form="♀ (female)" package=THT]
  1n4148 = Diode [package=diode-1n4148]

nets:
  5V: WeMos_D1_Mini1.5V, 5V.VCC, Composant1.VIN, GY1.pin1
  N1: WeMos_D1_Mini1.D1, GY1.pin3
  N2: WeMos_D1_Mini1.D2, GY1.pin4
  N3: WeMos_D1_Mini1.D4, Composant1.LRCLK
  N4: WeMos_D1_Mini1.D6, GY1.pin8
  N5: WeMos_D1_Mini1.D7, Composant4.IN
  N6: WeMos_D1_Mini1.D8, Composant1.BCLK
  GND: WeMos_D1_Mini1.G, 5V.GND, Composant4.GND, Composant1.GND, GY1.pin2
  N7: WeMos_D1_Mini1.RX, Composant1.DIN
  N8: SP1.+, Composant1.VO-
  N9: SP1.-, Composant1.VO+
  N10: Composant4.VDD, 1n4148.C

custom parts:
  NeoPixel Jewel: We fit seven of our tiny 5050 (5mm x 5mm) smart RGB LEDs onto a beautiful, round PCB with mounting holes and a chainable design to create what we think is our most elegant (and evening-wear appropriate) NeoPixel board yet. Use only one microcontroller pin to control as many as you can chain together! Each LED is addressable as the driver chip is inside the LED. Each one has ~18mA constant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
  Adafruit MAX98357A I2S 3W Class D Amplifier: Listen to this good news - we now have an all in one digital audio amp breakout board that works incredibly well with the Raspberry Pi! If you're looking for an easy and low cost way to get you digital sound files bumpin' then the MAX08357 I2S Amp Breakout is for you. It takes standard I2S digital audio input and, not only decodes it into analog, but also amplifies it directly into a speaker.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
  MPU-6050 Board GY-521: Acelerometro y Giroscopio MPU-6050 Board GY-521
